# Fritzing sketch Remyjr - schematic (saved by Fritzing 0.9.3b)

parts:
  SONAR1 = Maxbotix MaxSonar Ultrasonic Sensor
  SONAR2 = Maxbotix MaxSonar Ultrasonic Sensor
  SONAR3 = Maxbotix MaxSonar Ultrasonic Sensor
  SONAR5 = Maxbotix MaxSonar Ultrasonic Sensor
  SONAR6 = Maxbotix MaxSonar Ultrasonic Sensor
  SONAR7 = Maxbotix MaxSonar Ultrasonic Sensor
  SONAR8 = Maxbotix MaxSonar Ultrasonic Sensor
  Part2 = 9-DOF Absolute Orientation IMU Fusion Breakout - BNO055
  IC2 = MCP3008 8-channel 10-bit ADC [part_number=MCP3008]
  Part4 = Adafruit VL53L0X Time of Flight Distance Sensor [part_number="Adafruit #3317"]
  Part6 = 16-Channel 12-bit PCA9685 PWM/Servo Driver
  Part8 = Adafruit Analog 2-Axis Joystick [part_number="Adafruit #512"]
  IC3 = MCP3008 8-channel 10-bit ADC [part_number=MCP3008]
  Raspberry_Pi_1 = Raspberry Pi 3 [part_number=RPI-3-V1.2]
  IC4 = IC, SIP package, 6 pins [chip_label="Motor Drivers"]
  R1 = Resistor [tolerance=±5% resistance=1k package=THT]
  SONAR4 = Maxbotix MaxSonar Ultrasonic Sensor
  Part3 = Adafruit VL53L0X Time of Flight Distance Sensor [part_number="Adafruit #3317"]

nets:
  GND: SONAR1.GND, SONAR2.GND, SONAR3.GND, SONAR5.GND, SONAR6.GND, SONAR7.GND, SONAR8.GND, Part2.GND, IC2.no_name_yet#9, IC2.no_name_yet#14, Part4.GND, Part6.GND, Part8.GND, IC3.no_name_yet#9, IC3.no_name_yet#14, Raspberry_Pi_1.GND, IC4.pin2, IC4.pin5, SONAR4.GND, Part3.GND
  +5V: SONAR1.+5V, SONAR1.BW, SONAR2.+5V, SONAR2.BW, SONAR3.+5V, SONAR3.BW, SONAR5.+5V, SONAR5.BW, SONAR6.+5V, SONAR6.BW, SONAR7.+5V, SONAR7.BW, SONAR8.+5V, SONAR8.BW, Part2.5.0V, Part2.PS0_3V, IC2.no_name_yet#15, IC2.no_name_yet#16, Part4.VIN, Part6.VCC, Part8.VCC, IC3.no_name_yet#15, IC3.no_name_yet#16, Raspberry_Pi_1.3v3, Raspberry_Pi_1.3V3, SONAR4.+5V, SONAR4.BW, Part3.VIN
  N1: SONAR1.RX, SONAR6.RX, SONAR7.RX, Raspberry_Pi_1.GPIO5, R1.Pin_0, SONAR4.RX
  N2: SONAR1.AN, IC2.no_name_yet#2
  N3: SONAR2.RX, SONAR3.RX, SONAR5.RX, SONAR8.RX, SONAR4.TX
  N4: SONAR2.AN, IC2.no_name_yet#7
  N5: SONAR3.AN, IC2.no_name_yet#5
  N6: SONAR5.AN, IC2.no_name_yet#6
  N7: SONAR6.AN, IC2.no_name_yet#4
  N8: SONAR7.AN, IC2.no_name_yet#3
  N9: SONAR8.TX, R1.Pin_1
  N10: SONAR8.AN, IC2.no_name_yet#8
  N11: Part2.SDA_5V, Raspberry_Pi_1.GPIO15
  N12: Part2.SCL_5V, Raspberry_Pi_1.GPIO14
  N13: Part2.RST_5V, Raspberry_Pi_1.GPIO21
  N14: IC2.no_name_yet#1, SONAR4.AN
  N15: IC2.no_name_yet#10, Raspberry_Pi_1.GPIO4
  N16: IC2.no_name_yet#11, Raspberry_Pi_1.GPIO17
  N17: IC2.no_name_yet#12, Raspberry_Pi_1.GPIO27
  N18: IC2.no_name_yet#13, Raspberry_Pi_1.GPIO18
  N19: Part4.XSHUT, Raspberry_Pi_1.GPIO6
  N20: Part4.SCL, Part6.SCL, Raspberry_Pi_1.GPIO3, Part3.SCL
  N21: Part4.SDA, Part6.SDA, Raspberry_Pi_1.GPIO2, Part3.SDA
  N22: Part6.PWRIN, Raspberry_Pi_1.5V
  N23: Part6.0, IC4.pin6
  N24: Part6.1, IC4.pin3
  N25: Part6.V+, IC4.pin1, IC4.pin4
  N26: Part8.SWITCH, IC3.no_name_yet#8
  N27: Part8.YOUT, IC3.no_name_yet#6
  N28: Part8.XOUT, IC3.no_name_yet#7
  N29: IC3.no_name_yet#10, Raspberry_Pi_1.GPIO25
  N30: IC3.no_name_yet#11, Raspberry_Pi_1.GPIO24
  N31: IC3.no_name_yet#12, Raspberry_Pi_1.GPIO22
  N32: IC3.no_name_yet#13, Raspberry_Pi_1.GPIO23
  N33: Raspberry_Pi_1.GPIO12, Part3.XSHUT

custom parts:
  Maxbotix MaxSonar Ultrasonic Sensor: Maxbotix MaxSonar Ultrasonic Sensor LV-EZ0, LV-EZ1, LV-EZ2, LV-EZ3, LV-EZ4
  9-DOF Absolute Orientation IMU Fusion Breakout - BNO055: A MEMS accelerometer, magnetometer and gyroscope on a single die with a high speed ARM Cortex-M0 based processor to digest all the sensor data, abstract the sensor fusion and real time requirements away, and spit out data you can use in quaternions, Euler angles or vectors.
  Adafruit VL53L0X Time of Flight Distance Sensor: The VL53L0X is a Time of Flight distance sensor like no other you've used! The sensor contains a very tiny invisible laser source, and a matching sensor. The VL53L0X can detect the "time of flight", or how long the light has taken to bounce back to the sensor. Since it uses a very narrow light source, it is good for determining distance of only the surface directly in front of it. Unlike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
  16-Channel 12-bit PCA9685 PWM/Servo Driver: The Adafruit 16-Channel 12-bit PWM/Servo Driver will drive up to 16 servos over I2C with only 2 pins. The on-board PCA9685 PWM controller will drive all 16 channels simultaneously with no additional processing overhead. What's more, you can chain up to 62 of them to control up to 992 servos - all with the same 2 pins
  Adafruit Analog 2-Axis Joystick: This mini-kit makes it easy to mount a PSP/Xbox-like thumb joystick to your project. The thumbstick is an analog joystick - more accurate and sensitive than just 'directional' joysticks - with a 'press in to select' button. Since it's analog, you'll need two analog reading pins on your microcontroller to determine X and Y. Having an extra digital input will let you read the switch. The pack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
